# Fritzing sketch gardmon (saved by Fritzing 0.9.3b)
breadboards: 1

parts:
  DHT1 = DHT22 Humidity and Temperature Sensor
  ZS-042_RTC1 = ZS-042 RTC Module
  R1 = Resistor [tolerance=±5% resistance=100k package=THT]
  Power_plug1 = Power plug
  U2 = mystery part, 4 pins [chip_label="5V Convertor"]
  Part1 = Arduino Uno (Rev3)
  U1 = mystery part, 16 pins [chip_label=DMD]

nets:
  VDD: DHT1.VDD, ZS-042_RTC1.VCC, R1.Pin_0, U2.pin4
  N1: DHT1.DATA, R1.Pin_1, Part1.D2
  GND: DHT1.GND, ZS-042_RTC1.GND, Power_plug1.GND, U2.pin2, U2.pin3, Part1.GND, U1.pin1, U1.pin2, U1.pin3, U1.pin4, U1.pin5, U1.pin6, U1.pin7
  N2: ZS-042_RTC1.SDA, Part1.A4/SDA
  N3: ZS-042_RTC1.SCL, Part1.A5/SCL
  VCC: Power_plug1.VCC, U2.pin1, Part1.VIN
  N4: Part1.D10_PWM/SS, U1.pin8
  N5: Part1.D3_PWM, U1.pin14
  N6: Part1.D4, U1.pin13
  N7: Part1.D5_PWM, U1.pin12
  N8: Part1.D6_PWM, U1.pin10
  N9: Part1.D7, U1.pin9
